// Logisim project Exp_1.1.circ as structural Verilog: 1 circuit, main circuit main
module main (
  input  A,
  input  B
);

  wire and_1_out;

  and and_1 (and_1_out, A, B);
  LED led_1 (.in(and_1_out));
endmodule
