// Logisim project Exp_1.5.circ as structural Verilog: 1 circuit, main circuit main
module main (
  input  in_1,
  input  in_2
);

  wire nor_1_out;

  nor nor_1 (nor_1_out, in_1, in_2);
  LED led_1 (.in(nor_1_out));
endmodule
