// Logisim project asynchronous.circ as structural Verilog
module bit_up_counter (
  input  in_1,
  output Y0,
  output Y1,
  output Y2
);

  wire CLK_out;

  Clock CLK (.out(CLK_out));
  J_K_Flip_Flop #(.trigger("falling")) j_k_ff_1 (.J(in_1), .K(in_1), .clk(CLK_out), .Q(Y0));  // open: Qn, preset, reset
  J_K_Flip_Flop #(.trigger("falling")) j_k_ff_2 (.J(in_1), .K(in_1), .clk(Y0), .Q(Y1));  // open: Qn, preset, reset
  J_K_Flip_Flop #(.trigger("falling")) j_k_ff_3 (.J(in_1), .K(in_1), .clk(Y1), .Q(Y2));  // open: Qn, preset, reset
endmodule

module bit_down_counter (
  input  in_1,
  output Q0,
  output Q1,
  output Q2
);

  wire CLK_out, FFA_q, FFB_q;

  Clock CLK (.out(CLK_out));
  J_K_Flip_Flop #(.trigger("falling")) FFA (
    .J(in_1), .K(in_1), .clk(CLK_out), .Q(FFA_q), .Qn(Q0));  // open: preset, reset
  J_K_Flip_Flop #(.trigger("falling")) FFB (
    .J(in_1), .K(in_1), .clk(FFA_q), .Q(FFB_q), .Qn(Q1));  // open: preset, reset
  J_K_Flip_Flop #(.trigger("falling")) FFC (.J(in_1), .K(in_1), .clk(FFB_q), .Qn(Q2));  // open: Q, preset, reset
endmodule

module three_bit_up_down_counter (
  input  M,
  input  High,
  output Y2,
  output Y0,
  output Y1
);

  wire and_1_out, and_2_out, and_3_out, and_4_out, CLK_out, j_k_ff_1_qn, j_k_ff_2_qn, not_1_out, or_1_out,
       or_2_out;

  Clock CLK (.out(CLK_out));
  not not_1 (not_1_out, M);
  J_K_Flip_Flop j_k_ff_1 (.J(High), .K(High), .clk(CLK_out), .Q(Y0), .Qn(j_k_ff_1_qn));  // open: preset, reset
  and and_1 (and_1_out, M, Y0);
  and and_2 (and_2_out, not_1_out, j_k_ff_1_qn);
  or or_1 (or_1_out, and_1_out, and_2_out);
  J_K_Flip_Flop j_k_ff_2 (.J(High), .K(High), .clk(or_1_out), .Q(Y1), .Qn(j_k_ff_2_qn));  // open: preset, reset
  and and_3 (and_3_out, M, Y1);
  and and_4 (and_4_out, not_1_out, j_k_ff_2_qn);
  or or_2 (or_2_out, and_3_out, and_4_out);
  J_K_Flip_Flop j_k_ff_3 (.J(High), .K(High), .clk(or_2_out), .Q(Y2));  // open: Qn, preset, reset
endmodule
