// Logisim project synchronous.circ as structural Verilog
module three_bit_up (
  input  in_1,
  output Y0,
  output Y1,
  output Y2
);

  wire and_1_out, CLK_out;

  Clock CLK (.out(CLK_out));
  J_K_Flip_Flop FF00 (.J(in_1), .K(in_1), .clk(CLK_out), .Q(Y0));  // open: Qn, preset, reset
  J_K_Flip_Flop FF01 (.J(Y0), .K(Y0), .clk(CLK_out), .Q(Y1));  // open: Qn, preset, reset
  and and_1 (and_1_out, Y0, Y1);
  J_K_Flip_Flop FF03 (.J(and_1_out), .K(and_1_out), .clk(CLK_out), .Q(Y2));  // open: Qn, preset, reset
endmodule

module three_bit_down (
  input  in_1,
  output Y0,
  output Y1,
  output Y2
);

  wire and_1_out, CLK_out, FF00_qn, FF01_qn;

  Clock CLK (.out(CLK_out));
  J_K_Flip_Flop FF00 (.J(in_1), .K(in_1), .clk(CLK_out), .Q(Y0), .Qn(FF00_qn));  // open: preset, reset
  J_K_Flip_Flop FF01 (.J(FF00_qn), .K(FF00_qn), .clk(CLK_out), .Q(Y1), .Qn(FF01_qn));  // open: preset, reset
  and and_1 (and_1_out, FF01_qn, FF00_qn);
  J_K_Flip_Flop FF03 (.J(and_1_out), .K(and_1_out), .clk(CLK_out), .Q(Y2));  // open: Qn, preset, reset
endmodule
