// Logisim project Exp_2.1.circ as structural Verilog: 1 circuit, main circuit main
module main (
  input  A,
  input  B,
  input  in_3,
  input  in_4
);

  wire nand_1_out, not_1_out, not_2_out, or_1_out;

  not not_1 (not_1_out, A);
  not not_2 (not_2_out, B);
  nand nand_1 (nand_1_out, in_3, in_4);
  or or_1 (or_1_out, not_1_out, not_2_out);
  LED led_1 (.in(nand_1_out));
  LED F (.in(or_1_out));
endmodule
