// Logisim project Exp_2.2.circ as structural Verilog: 1 circuit, main circuit main
module main (
  input  in_1,
  input  in_2,
  input  in_3,
  input  in_4
);

  wire and_1_out, nor_1_out, not_1_out, not_2_out;

  not not_1 (not_1_out, in_1);
  not not_2 (not_2_out, in_2);
  and and_1 (and_1_out, not_1_out, not_2_out);
  nor nor_1 (nor_1_out, in_3, in_4);
  LED led_1 (.in(and_1_out));
  LED led_2 (.in(nor_1_out));
endmodule
