// Logisim project using_exor_basic_gates.circ as structural Verilog: 1 circuit, main circuit main
module main (
  input  A,
  input  B,
  input  C
);

  wire and_1_out, and_2_out, or_1_out, xor_1_out, xor_2_out;

  and and_1 (and_1_out, B, A);
  xor xor_1 (xor_1_out, A, B);
  and and_2 (and_2_out, C, xor_1_out);
  xor xor_2 (xor_2_out, xor_1_out, C);
  LED S (.in(xor_2_out));
  or or_1 (or_1_out, and_2_out, and_1_out);
  LED Cout (.in(or_1_out));
endmodule
