// Logisim project Exp_5.2.circ as structural Verilog: 1 circuit, main circuit main
module main (
  input  G3,
  input  G2,
  input  G1,
  input  G0
);

  wire xor_1_out, xor_2_out, xor_3_out;

  xor xor_1 (xor_1_out, G3, G2);
  xor xor_2 (xor_2_out, xor_1_out, G1);
  xor xor_3 (xor_3_out, xor_2_out, G0);
  LED B3 (.in(G3));
  LED B2 (.in(xor_1_out));
  LED B1 (.in(xor_2_out));
  LED B0 (.in(xor_3_out));
endmodule
