// Logisim project demultiplexers.circ as structural Verilog: 1 circuit, main circuit main
module main (
  input  S0,
  input  S1
);

  wire and_1_out, and_2_out, and_3_out, and_4_out, DATA_out, not_1_out, not_2_out;

  Button DATA (.out(DATA_out));
  not not_1 (not_1_out, S0);
  not not_2 (not_2_out, S1);
  and and_1 (and_1_out, not_1_out, not_2_out, DATA_out);
  and and_2 (and_2_out, S0, not_2_out, DATA_out);
  and and_3 (and_3_out, not_1_out, S1, DATA_out);
  and and_4 (and_4_out, S0, S1, DATA_out);
  LED D0 (.in(and_1_out));
  LED D1 (.in(and_2_out));
  LED D2 (.in(and_3_out));
  LED D3 (.in(and_4_out));
endmodule
