// Logisim project multiplexers.circ as structural Verilog: 1 circuit, main circuit main
module main (
  input  S0,
  input  S1
);

  wire and_1_out, and_2_out, and_3_out, and_4_out, D0_out, D1_out, D2_out, D3_out, not_1_out, not_2_out,
       or_1_out;

  Button D0 (.out(D0_out));
  Button D1 (.out(D1_out));
  Button D2 (.out(D2_out));
  Button D3 (.out(D3_out));
  not not_1 (not_1_out, S1);
  not not_2 (not_2_out, S0);
  and and_1 (and_1_out, D0_out, not_1_out, not_2_out);
  and and_2 (and_2_out, D1_out, not_1_out, S0);
  and and_3 (and_3_out, D2_out, S1, not_2_out);
  and and_4 (and_4_out, D3_out, S1, S0);
  or or_1 (or_1_out, and_1_out, and_2_out, and_3_out, and_4_out);
  LED Y (.in(or_1_out));
endmodule
