// Logisim project bcd_adder.circ as structural Verilog: 4 circuits, main circuit main
module main (
  input  A3,
  input  A2,
  input  A1,
  input  A0,
  input  B3,
  input  B2,
  input  B1,
  input  B0,
  output MSD,
  output Cout,
  output S3,
  output S2,
  output S1,
  output S0
);

  wire four_bit_adder_1_cout, four_bit_adder_1_s0, four_bit_adder_1_s1, four_bit_adder_1_s2,
       four_bit_adder_1_s3, nand_2_out, nand_3_out, nand_4_out;

  nand nand_1 (MSD, nand_2_out, nand_3_out, nand_4_out);
  nand nand_2 (nand_2_out, four_bit_adder_1_cout, four_bit_adder_1_cout);
  // NAND_Gate nand_3 has open pins: out=nand_3_out
  // NAND_Gate nand_4 has open pins: out=nand_4_out
  four_bit_adder four_bit_adder_1 (
    .Cin(1'b0), .B0(B0), .B1(B1), .B2(B2), .B3(B3), .A0(A0), .A1(A1), .A2(A2), .A3(A3),
    .S0(four_bit_adder_1_s0), .S1(four_bit_adder_1_s1), .S2(four_bit_adder_1_s2), .S3(four_bit_adder_1_s3),
    .Cout(four_bit_adder_1_cout));
  four_bit_adder four_bit_adder_2 (
    .Cin(1'b0), .B0(four_bit_adder_1_s0), .B1(four_bit_adder_1_s1), .B2(four_bit_adder_1_s2),
    .B3(four_bit_adder_1_s3), .A0(1'b0), .A1(MSD), .A2(MSD), .A3(1'b0), .S0(S0), .S1(S1), .S2(S2), .S3(S3),
    .Cout(Cout));
endmodule

module fulladder (
  input  A,
  input  B,
  input  C,
  output S,
  output Cout
);

  wire and_1_out, and_2_out, xor_1_out;

  and and_1 (and_1_out, B, A);
  xor xor_1 (xor_1_out, A, B);
  and and_2 (and_2_out, C, xor_1_out);
  xor xor_2 (S, xor_1_out, C);
  or or_1 (Cout, and_2_out, and_1_out);
endmodule

module four_bit_adder (
  input  Cin,
  input  B0,
  input  B1,
  input  B2,
  input  B3,
  input  A0,
  input  A1,
  input  A2,
  input  A3,
  output S0,
  output S1,
  output S2,
  output S3,
  output Cout
);

  wire fulladder_1_cout, fulladder_2_cout, fulladder_3_cout;

  fulladder fulladder_1 (.A(A0), .B(B0), .C(Cin), .S(S0), .Cout(fulladder_1_cout));
  fulladder fulladder_2 (.A(A1), .B(B1), .C(fulladder_1_cout), .S(S1), .Cout(fulladder_2_cout));
  fulladder fulladder_3 (.A(A2), .B(B2), .C(fulladder_2_cout), .S(S2), .Cout(fulladder_3_cout));
  fulladder fulladder_4 (.A(A3), .B(B3), .C(fulladder_3_cout), .S(S3), .Cout(Cout));
endmodule

module fourbitadder (
  input  B3,
  input  B2,
  input  B1,
  input  B0,
  input  Cin,
  input  A3,
  input  A2,
  input  A1,
  input  A0,
  output Cout,
  output S3,
  output S2,
  output S1,
  output S0
);

  wire xor_1_out, xor_2_out, xor_3_out, xor_4_out;

  xor xor_1 (xor_1_out, B3, Cin);
  xor xor_2 (xor_2_out, B2, Cin);
  xor xor_3 (xor_3_out, B1, Cin);
  four_bit_adder four_bit_adder_1 (
    .Cin(Cin), .B0(xor_4_out), .B1(xor_3_out), .B2(xor_2_out), .B3(xor_1_out), .A0(A0), .A1(A1), .A2(A2),
    .A3(A3), .S0(S0), .S1(S1), .S2(S2), .S3(S3), .Cout(Cout));
  xor xor_4 (xor_4_out, B0, Cin);
endmodule
