// Logisim project comparator..circ as structural Verilog: 1 circuit, main circuit main
module main (
  input  A1,
  input  A0,
  input  B1,
  input  B0,
  input  in_5,
  input  in_6,
  input  in_7,
  output out_8,
  output out_9,
  output out_10
);

  _7485 u_7485_1 (
    .pin2(in_5), .pin3(in_6), .pin4(in_7), .pin5(out_8), .pin6(out_9), .pin7(out_10), .pin12(A1), .pin11(B1),
    .pin10(A0), .pin9(B0));  // open: pin1, pin15, pin14, pin13
endmodule
